// Digital circuit Ejemplos bancos de Memorias.dig as structural Verilog
module Ejemplos_bancos_de_Memorias (
  input  [13:0] in_1,
  input  in_2,
  input  in_3,
  input  [1:0] in_4,
  input  [7:0] in_5,
  input  [9:0] in_6,
  input  in_7,
  input  in_8,
  input  [1:0] in_9,
  input  [7:0] in_10,
  input  [7:0] in_11,
  input  in_13,
  input  in_14,
  output [7:0] out_12,
  output [7:0] out_15,
  output [7:0] out_16
);

  wire decoder_1_out_0, decoder_1_out_1, decoder_1_out_2, decoder_1_out_3, decoder_2_out_0, decoder_2_out_1,
       decoder_2_out_2, decoder_2_out_3;

  Decoder #(.Selector_Bits(2)) decoder_1 (
    .sel(in_4), .out_0(decoder_1_out_0), .out_1(decoder_1_out_1), .out_2(decoder_1_out_2),
    .out_3(decoder_1_out_3));
  assign out_12 = in_13 ? in_5 : 8'bz;  // Driver driver_1
  RAMSinglePortSel #(.AddrBits(14), .Bits(8)) ramsingleportsel_1 (
    .A(in_1), .CS(decoder_1_out_3), .WE(in_3), .OE(in_2), .D(out_12));
  RAMSinglePortSel #(.AddrBits(14), .Bits(8)) ramsingleportsel_2 (
    .A(in_1), .CS(decoder_1_out_2), .WE(in_3), .OE(in_2), .D(out_12));
  RAMSinglePortSel #(.AddrBits(14), .Bits(8)) ramsingleportsel_3 (
    .A(in_1), .CS(decoder_1_out_1), .WE(in_3), .OE(in_2), .D(out_12));
  RAMSinglePortSel #(.AddrBits(14), .Bits(8)) ramsingleportsel_4 (
    .A(in_1), .CS(decoder_1_out_0), .WE(in_3), .OE(in_2), .D(out_12));
  Decoder #(.Selector_Bits(2)) decoder_2 (
    .sel(in_9), .out_0(decoder_2_out_0), .out_1(decoder_2_out_1), .out_2(decoder_2_out_2),
    .out_3(decoder_2_out_3));
  assign out_16 = in_14 ? in_10 : 8'bz;  // Driver driver_2
  assign out_15 = in_14 ? in_11 : 8'bz;  // Driver driver_3
  RAMSinglePortSel #(.AddrBits(10), .Bits(8)) ramsingleportsel_5 (
    .A(in_6), .CS(decoder_2_out_3), .WE(in_8), .OE(in_7), .D(out_16));
  RAMSinglePortSel #(.AddrBits(10), .Bits(8)) ramsingleportsel_6 (
    .A(in_6), .CS(decoder_2_out_3), .WE(in_8), .OE(in_7), .D(out_15));
  RAMSinglePortSel #(.AddrBits(10), .Bits(8)) ramsingleportsel_7 (
    .A(in_6), .CS(decoder_2_out_2), .WE(in_8), .OE(in_7), .D(out_16));
  RAMSinglePortSel #(.AddrBits(10), .Bits(8)) ramsingleportsel_8 (
    .A(in_6), .CS(decoder_2_out_2), .WE(in_8), .OE(in_7), .D(out_15));
  RAMSinglePortSel #(.AddrBits(10), .Bits(8)) ramsingleportsel_9 (
    .A(in_6), .CS(decoder_2_out_1), .WE(in_8), .OE(in_7), .D(out_16));
  RAMSinglePortSel #(.AddrBits(10), .Bits(8)) ramsingleportsel_10 (
    .A(in_6), .CS(decoder_2_out_1), .WE(in_8), .OE(in_7), .D(out_15));
  RAMSinglePortSel #(.AddrBits(10), .Bits(8)) ramsingleportsel_11 (
    .A(in_6), .CS(decoder_2_out_0), .WE(in_8), .OE(in_7), .D(out_16));
  RAMSinglePortSel #(.AddrBits(10), .Bits(8)) ramsingleportsel_12 (
    .A(in_6), .CS(decoder_2_out_0), .WE(in_8), .OE(in_7), .D(out_15));

  // Notes on the sheet:
  //   A15-A14
  //   A13-A0
  //   Escritura
  //   Lectura
  //   D7-D0
  //   64K x 8 con chips de 16K x 8
  //   49152
  //   65535
  //   Direcciones
  //   32768
  //   49151
  //   16384
  //   32767
  //   D15-D8
  //   A11-A10
  //   A9-A0
  //   4K x 16 con chips de 1K x 8
  //   3072
  //   4095
  //   2048
  //   3071
  //   1024
  //   2047
  //   0
  //   1023
endmodule
